# Fritzing sketch 2023-01-06-V2_schematics (saved by Fritzing 0.9.10b)
breadboards: 1

parts:
  Arduino_Uno = Arduino Uno (Rev3) - ICSP
  MPU6050 = InvenSense MPU6050
  Vibration_Motor = Vibration Motor- ROB-08449 [package=vibe-motor-10mm]
  R1 = Resistor [tolerance=±5% resistance=220 package="2010 [SMD]"]
  LED = smd LED [color="Red (633nm)" package="0603 [SMD]"]

nets (from the breadboard view):
  N1: Arduino_Uno.A4/SDA, MPU6050.SDA
  N2: Arduino_Uno.A5/SCL, MPU6050.SCL
  GND: Arduino_Uno.GND, MPU6050.GND, Vibration_Motor.+, LED.anode
  N3: Arduino_Uno.D9_PWM, Vibration_Motor.-
  N4: Arduino_Uno.D6_PWM, R1.Pin_0
  5V: Arduino_Uno.5V, MPU6050.VCC
  N5: R1.Pin_1, LED.cathode
