# Fritzing sketch 2023-01-06_schematics (saved by Fritzing 0.9.10b)
breadboards: 1

parts:
  Composant1 = Arduino Uno (Rev3) - ICSP
  Composant2 = InvenSense MPU6050
  U1 = Vibration Motor- ROB-08449 [package=vibe-motor-10mm]
  LED1 = smd LED [color="Red (633nm)" package="0603 [SMD]"]
  R1 = Resistor [tolerance=±5% resistance=220 package="2010 [SMD]"]

nets:
  N1: Composant1.A4/SDA, Composant2.SDA
  N2: Composant1.A5/SCL, Composant2.SCL
  N3: Composant1.D9_PWM, U1.-
  GND: Composant1.GND, Composant2.GND, U1.+, LED1.anode
  N4: Composant1.D6_PWM, R1.Pin_0
  5V: Composant1.5V, Composant2.VCC
  N5: LED1.cathode, R1.Pin_1
